# Fritzing sketch arduino-section (saved by Fritzing 0.9.6b)
breadboards: 1

parts:
  Part1 = LCD1602-I2C
  Part3 = Arduino Uno (Rev3) - ICSP
  Part2 = Soil Moisture Sensor

nets:
  GND: Part1.GND, Part3.GND, Part2.GND
  VCC: Part1.VCC, Part3.5V, Part2.VCC
  N1: Part1.SDA, Part3.A4/SDA
  N2: Part1.SCL, Part3.A5/SCL
  N3: Part3.A0, Part2.SIG

custom parts:
  LCD1602-I2C: A standard character display, usually with 2x16 characters. Comes in many colors with LCM1602 IIC attached.
