# Fritzing sketch wifi-module-section (saved by Fritzing 0.9.6b)
breadboards: 1

parts:
  Part2 = Soil Moisture Sensor
  U1 = ESP8266 NodeMCU LoLin module

nets:
  N1: Part2.SIG, U1.A0
  GND: Part2.GND, U1.GND

custom parts:
  ESP8266 NodeMCU LoLin module: ESP8266 based NodeMCU
